// Logisim project SAP-1.circ as structural Verilog: 13 circuits, main circuit main
module main (
  input  a3,
  input  a2,
  input  a1,
  input  a0,
  input  d7,
  input  d6,
  input  d5,
  input  d4,
  input  R1orP0,
  input  d3,
  input  d2,
  input  d1,
  input  d0,
  input  wr,
  input  in_15,
  input  in_16,
  input  in_17
);

  wire acumulator_1_aluout0, acumulator_1_aluout1, acumulator_1_aluout2, acumulator_1_aluout3,
       acumulator_1_aluout4, acumulator_1_aluout5, acumulator_1_aluout6, acumulator_1_aluout7, AI, AO, BI,
       bregister_1_a0, bregister_1_a1, bregister_1_a2, bregister_1_a3, bregister_1_a4, bregister_1_a5,
       bregister_1_a6, bregister_1_a7, CE, CLK, clock_1_out, CO, controlled_buffer_2_out,
       controllersequencer_1_hlt, controllersequencer_1_stpclk, EO, HLT, II, inputunit_1_runprog,
       inputunit_1_wro, insturductionregister_1_c0, insturductionregister_1_c1, insturductionregister_1_c2,
       insturductionregister_1_c3, IO, mar_1_m0out, mar_1_m1out, mar_1_m2out, mar_1_m3out, MI, not_1_out,
       not_2_out, OI, or_1_out, or_3_out, RO, SU;
  wire [3:0] adressselector_1_s0, inputunit_1_aout, outregister_1_a0, outregister_1_a4;
  wire [7:0] inputunit_1_dout, insturductionregister_1_bus0, ram_1_dout;

  InputUnit inputunit_1 (
    .wr(wr), .d7(d7), .d6(d6), .d5(d5), .d4(d4), .d3(d3), .d2(d2), .d1(d1), .d0(d0), .a3(a3), .a2(a2),
    .a1(a1), .a0(a0), .RunProgIn(R1orP0), .wro(inputunit_1_wro), .Dout(inputunit_1_dout),
    .Aout(inputunit_1_aout), .RunProg(inputunit_1_runprog));
  RAM #(.addrWidth(4)) ram_1 (
    .addr(adressselector_1_s0), .we(inputunit_1_wro), .oe(RO), .clk(or_1_out), .din(inputunit_1_dout),
    .dout(ram_1_dout));
  or or_1 (or_1_out, RO, inputunit_1_wro);
  not not_1 (not_1_out, CLK);
  ControllerSequencer controllersequencer_1 (
    .A3(insturductionregister_1_c3), .A2(insturductionregister_1_c2), .A1(insturductionregister_1_c1),
    .A0(insturductionregister_1_c0), .CLK(not_1_out), .RST(HLT), .HRDRST(in_15), .CO(CO), .AO(AO), .CE(CE),
    .OI(OI), .II(II), .IO(IO), .MI(MI), .RO(RO), .AI(AI), .BI(BI), .HLT(controllersequencer_1_hlt), .EO(EO),
    .stpclk(controllersequencer_1_stpclk), .SU(SU));
  AdressSelector adressselector_1 (
    .R1orP0(inputunit_1_runprog), .A3(inputunit_1_aout[3]), .A2(inputunit_1_aout[2]),
    .A1(inputunit_1_aout[1]), .A0(inputunit_1_aout[0]), .B3(mar_1_m3out), .B2(mar_1_m2out), .B1(mar_1_m1out),
    .B0(mar_1_m0out), .S3(adressselector_1_s0[3]), .S2(adressselector_1_s0[2]), .S1(adressselector_1_s0[1]),
    .S0(adressselector_1_s0[0]));
  InsturductionRegister insturductionregister_1 (
    .B7(insturductionregister_1_bus0[7]), .B6(insturductionregister_1_bus0[6]),
    .B5(insturductionregister_1_bus0[5]), .B4(insturductionregister_1_bus0[4]),
    .B3(insturductionregister_1_bus0[3]), .B2(insturductionregister_1_bus0[2]),
    .B1(insturductionregister_1_bus0[1]), .II(II), .B0(insturductionregister_1_bus0[0]), .CLK(CLK),
    .RST(HLT), .IO(IO), .BUS1(insturductionregister_1_bus0[1]), .BUS0(insturductionregister_1_bus0[0]),
    .C3(insturductionregister_1_c3), .C2(insturductionregister_1_c2), .C1(insturductionregister_1_c1),
    .C0(insturductionregister_1_c0), .BUS3(insturductionregister_1_bus0[3]),
    .BUS2(insturductionregister_1_bus0[2]));
  MAR mar_1 (
    .MI(MI), .CLK(CLK), .M0(insturductionregister_1_bus0[0]), .M1(insturductionregister_1_bus0[1]),
    .M2(insturductionregister_1_bus0[2]), .M3(insturductionregister_1_bus0[3]), .M0out(mar_1_m0out),
    .M1out(mar_1_m1out), .M2out(mar_1_m2out), .M3out(mar_1_m3out));
  assign insturductionregister_1_bus0 = RO ? ram_1_dout : 8'bz;  // Controlled_Buffer controlled_buffer_1
  or or_2 (HLT, controllersequencer_1_hlt, in_15);
  ProgramCounter programcounter_1 (
    .RES(HLT), .CO(CO), .CE(CE), .CLK(CLK), .x3(insturductionregister_1_bus0[3]),
    .x2(insturductionregister_1_bus0[2]), .x1(insturductionregister_1_bus0[1]),
    .x0(insturductionregister_1_bus0[0]));
  LED led_1 (.in(insturductionregister_1_bus0[7]));
  LED led_2 (.in(insturductionregister_1_bus0[6]));
  Clock clock_1 (.out(clock_1_out));
  assign controlled_buffer_2_out = in_16 ? clock_1_out : 1'bz;  // Controlled_Buffer controlled_buffer_2
  or or_3 (or_3_out, in_17, controlled_buffer_2_out);
  not not_2 (not_2_out, controllersequencer_1_stpclk);
  and and_1 (CLK, not_2_out, or_3_out);
  LED led_3 (.in(insturductionregister_1_bus0[5]));
  LED led_4 (.in(insturductionregister_1_bus0[4]));
  LED led_5 (.in(insturductionregister_1_bus0[3]));
  LED led_6 (.in(insturductionregister_1_bus0[2]));
  LED led_7 (.in(insturductionregister_1_bus0[1]));
  LED led_8 (.in(insturductionregister_1_bus0[0]));
  ALU alu_1 (
    .A3(acumulator_1_aluout3), .A2(acumulator_1_aluout2), .A1(acumulator_1_aluout1),
    .A0(acumulator_1_aluout0), .EO(EO), .SU(SU), .B7(bregister_1_a7), .B6(bregister_1_a6),
    .B5(bregister_1_a5), .B4(bregister_1_a4), .B3(bregister_1_a3), .B2(bregister_1_a2), .B1(bregister_1_a1),
    .B0(bregister_1_a0), .A7(acumulator_1_aluout7), .A6(acumulator_1_aluout6), .A5(acumulator_1_aluout5),
    .A4(acumulator_1_aluout4), .Bo4(insturductionregister_1_bus0[4]), .Bo5(insturductionregister_1_bus0[5]),
    .Bo6(insturductionregister_1_bus0[6]), .Bo7(insturductionregister_1_bus0[7]),
    .Bo0(insturductionregister_1_bus0[0]), .Bo1(insturductionregister_1_bus0[1]),
    .Bo2(insturductionregister_1_bus0[2]), .Bo3(insturductionregister_1_bus0[3]));
  Bregister bregister_1 (
    .B7(insturductionregister_1_bus0[7]), .B6(insturductionregister_1_bus0[6]),
    .B5(insturductionregister_1_bus0[5]), .B4(insturductionregister_1_bus0[4]),
    .B3(insturductionregister_1_bus0[3]), .B2(insturductionregister_1_bus0[2]),
    .B1(insturductionregister_1_bus0[1]), .BI(BI), .B0(insturductionregister_1_bus0[0]), .CLK(CLK),
    .A7(bregister_1_a7), .A6(bregister_1_a6), .A5(bregister_1_a5), .A4(bregister_1_a4), .A3(bregister_1_a3),
    .A2(bregister_1_a2), .A1(bregister_1_a1), .A0(bregister_1_a0));
  Acumulator acumulator_1 (
    .AI(AI), .clk(CLK), .AO(AO), .Bin7(insturductionregister_1_bus0[7]),
    .Bin6(insturductionregister_1_bus0[6]), .Bin5(insturductionregister_1_bus0[5]),
    .Bin4(insturductionregister_1_bus0[4]), .Bin3(insturductionregister_1_bus0[3]),
    .Bin2(insturductionregister_1_bus0[2]), .Bin1(insturductionregister_1_bus0[1]),
    .Bin0(insturductionregister_1_bus0[0]), .ALUout7(acumulator_1_aluout7),
    .Bout7(insturductionregister_1_bus0[7]), .ALUout6(acumulator_1_aluout6),
    .Bout6(insturductionregister_1_bus0[6]), .ALUout5(acumulator_1_aluout5),
    .Bout5(insturductionregister_1_bus0[5]), .ALUout4(acumulator_1_aluout4),
    .Bout4(insturductionregister_1_bus0[4]), .ALUout3(acumulator_1_aluout3),
    .Bout3(insturductionregister_1_bus0[3]), .ALUout2(acumulator_1_aluout2),
    .Bout2(insturductionregister_1_bus0[2]), .ALUout1(acumulator_1_aluout1),
    .Bout1(insturductionregister_1_bus0[1]), .ALUout0(acumulator_1_aluout0),
    .Bout0(insturductionregister_1_bus0[0]));
  OutRegister outregister_1 (
    .B3(insturductionregister_1_bus0[3]), .B2(insturductionregister_1_bus0[2]),
    .B1(insturductionregister_1_bus0[1]), .B0(insturductionregister_1_bus0[0]), .CLK(CLK), .OI(OI),
    .rst(HLT), .B7(insturductionregister_1_bus0[7]), .B6(insturductionregister_1_bus0[6]),
    .B5(insturductionregister_1_bus0[5]), .B4(insturductionregister_1_bus0[4]), .A6(outregister_1_a4[2]),
    .A5(outregister_1_a4[1]), .A4(outregister_1_a4[0]), .A3(outregister_1_a0[3]), .A2(outregister_1_a0[2]),
    .A1(outregister_1_a0[1]), .A0(outregister_1_a0[0]), .A7(outregister_1_a4[3]));
  Hex_Digit_Display hex_digit_display_1 (.value(outregister_1_a4));  // open: dp
  Hex_Digit_Display hex_digit_display_2 (.value(outregister_1_a0));  // open: dp

  // Notes on the sheet:
  //   B7 B6 B5 B4 B3 B2 B1 B0
endmodule

module HA (
  input  A,
  input  B,
  output out_3,
  output out_4
);

  xor xor_1 (out_3, A, B);
  and and_1 (out_4, A, B);
endmodule

module PC (
  input  CO,
  input  CE,
  input  CLK,
  input  RES,
  output out_5,
  output out_6,
  output out_7,
  output out_8
);

  wire and_1_out, and_2_out, j_k_ff_1_q, j_k_ff_2_q, j_k_ff_3_q, j_k_ff_4_q;

  J_K_Flip_Flop j_k_ff_1 (.J(CE), .K(CE), .clk(CLK), .Q(j_k_ff_1_q), .reset(RES));  // open: Qn, preset
  J_K_Flip_Flop j_k_ff_2 (.J(j_k_ff_1_q), .K(j_k_ff_1_q), .clk(CLK), .Q(j_k_ff_2_q), .reset(RES));  // open: Qn, preset
  J_K_Flip_Flop j_k_ff_3 (.J(and_1_out), .K(and_1_out), .clk(CLK), .Q(j_k_ff_3_q), .reset(RES));  // open: Qn, preset
  J_K_Flip_Flop j_k_ff_4 (.J(and_2_out), .K(and_2_out), .clk(CLK), .Q(j_k_ff_4_q), .reset(RES));  // open: Qn, preset
  and and_1 (and_1_out, j_k_ff_2_q, j_k_ff_1_q);
  and and_2 (and_2_out, j_k_ff_3_q, and_1_out);
  assign out_5 = CO ? j_k_ff_1_q : 1'bz;  // Controlled_Buffer controlled_buffer_1
  assign out_6 = CO ? j_k_ff_2_q : 1'bz;  // Controlled_Buffer controlled_buffer_2
  assign out_7 = CO ? j_k_ff_3_q : 1'bz;  // Controlled_Buffer controlled_buffer_3
  assign out_8 = CO ? j_k_ff_4_q : 1'bz;  // Controlled_Buffer controlled_buffer_4
endmodule

module ProgramCounter (
  input  CO,
  input  CE,
  input  CLK,
  input  RES,
  output x3,
  output x2,
  output x1,
  output x0
);

  wire and_1_out, and_2_out, and_3_out, j_k_ff_1_q, j_k_ff_2_q, j_k_ff_3_q, j_k_ff_4_q;

  and and_1 (and_1_out, CE, CLK);
  J_K_Flip_Flop j_k_ff_1 (.J(CE), .K(CE), .clk(and_1_out), .Q(j_k_ff_1_q), .reset(RES));  // open: Qn, preset
  J_K_Flip_Flop j_k_ff_2 (
    .J(j_k_ff_1_q), .K(j_k_ff_1_q), .clk(and_1_out), .Q(j_k_ff_2_q), .reset(RES));  // open: Qn, preset
  J_K_Flip_Flop j_k_ff_3 (
    .J(and_2_out), .K(and_2_out), .clk(and_1_out), .Q(j_k_ff_3_q), .reset(RES));  // open: Qn, preset
  J_K_Flip_Flop j_k_ff_4 (
    .J(and_3_out), .K(and_3_out), .clk(and_1_out), .Q(j_k_ff_4_q), .reset(RES));  // open: Qn, preset
  and and_2 (and_2_out, j_k_ff_2_q, j_k_ff_1_q);
  and and_3 (and_3_out, j_k_ff_3_q, and_2_out);
  assign x0 = CO ? j_k_ff_1_q : 1'bz;  // Controlled_Buffer controlled_buffer_1
  assign x1 = CO ? j_k_ff_2_q : 1'bz;  // Controlled_Buffer controlled_buffer_2
  assign x2 = CO ? j_k_ff_3_q : 1'bz;  // Controlled_Buffer controlled_buffer_3
  assign x3 = CO ? j_k_ff_4_q : 1'bz;  // Controlled_Buffer controlled_buffer_4
endmodule

module InputUnit (
  input  RunProgIn,
  input  wr,
  input  d7,
  input  d6,
  input  d5,
  input  d4,
  input  d3,
  input  d2,
  input  d1,
  input  d0,
  input  a3,
  input  a2,
  input  a1,
  input  a0,
  output wro,
  output RunProg,
  output [7:0] Dout,
  output [3:0] Aout
);


  assign Aout = {a3, a2, a1, a0};
  assign Dout = {d7, d6, d5, d4, d3, d2, d1, d0};
  assign RunProg = RunProgIn;
  assign wro = wr;
endmodule

module MAR (
  input  CLK,
  input  MI,
  input  M0,
  input  M1,
  input  M2,
  input  M3,
  output M0out,
  output M1out,
  output M2out,
  output M3out
);

  wire controlled_buffer_1_out, controlled_buffer_2_out, controlled_buffer_3_out, controlled_buffer_4_out;

  assign controlled_buffer_1_out = MI ? M0 : 1'bz;  // Controlled_Buffer controlled_buffer_1
  assign controlled_buffer_2_out = MI ? M1 : 1'bz;  // Controlled_Buffer controlled_buffer_2
  assign controlled_buffer_3_out = MI ? M2 : 1'bz;  // Controlled_Buffer controlled_buffer_3
  assign controlled_buffer_4_out = MI ? M3 : 1'bz;  // Controlled_Buffer controlled_buffer_4
  D_Flip_Flop d_ff_1 (.D(controlled_buffer_1_out), .clk(CLK), .Q(M0out));  // open: Qn, preset, reset
  D_Flip_Flop d_ff_2 (.D(controlled_buffer_2_out), .clk(CLK), .Q(M1out));  // open: Qn, preset, reset
  D_Flip_Flop d_ff_3 (.D(controlled_buffer_3_out), .clk(CLK), .Q(M2out));  // open: Qn, preset, reset
  D_Flip_Flop d_ff_4 (.D(controlled_buffer_4_out), .clk(CLK), .Q(M3out));  // open: Qn, preset, reset
endmodule

module AdressSelector (
  input  A3,
  input  A2,
  input  A1,
  input  A0,
  input  B3,
  input  B2,
  input  B1,
  input  B0,
  input  R1orP0,
  output S3,
  output S2,
  output S1,
  output S0
);

  wire not_1_out;

  assign S3 = R1orP0 ? A3 : 1'bz;  // Controlled_Buffer controlled_buffer_1
  not not_1 (not_1_out, R1orP0);
  assign S2 = R1orP0 ? A2 : 1'bz;  // Controlled_Buffer controlled_buffer_2
  assign S1 = R1orP0 ? A1 : 1'bz;  // Controlled_Buffer controlled_buffer_3
  assign S0 = R1orP0 ? A0 : 1'bz;  // Controlled_Buffer controlled_buffer_4
  assign S3 = not_1_out ? B3 : 1'bz;  // Controlled_Buffer controlled_buffer_5
  assign S2 = not_1_out ? B2 : 1'bz;  // Controlled_Buffer controlled_buffer_6
  assign S1 = not_1_out ? B1 : 1'bz;  // Controlled_Buffer controlled_buffer_7
  assign S0 = not_1_out ? B0 : 1'bz;  // Controlled_Buffer controlled_buffer_8
endmodule

module Acumulator (
  input  Bin7,
  input  Bin6,
  input  Bin5,
  input  Bin4,
  input  Bin3,
  input  Bin2,
  input  Bin1,
  input  Bin0,
  input  AI,
  input  clk,
  input  AO,
  output ALUout7,
  output ALUout6,
  output ALUout4,
  output ALUout5,
  output ALUout3,
  output ALUout1,
  output ALUout0,
  output ALUout2,
  output Bout7,
  output Bout6,
  output Bout5,
  output Bout4,
  output Bout3,
  output Bout2,
  output Bout1,
  output Bout0
);

  wire controlled_buffer_3_out, controlled_buffer_5_out, controlled_buffer_7_out, controlled_buffer_9_out,
       controlled_buffer_11_out, controlled_buffer_13_out, controlled_buffer_15_out, controlled_buffer_16_out;

  assign Bout7 = AO ? ALUout7 : 1'bz;  // Controlled_Buffer controlled_buffer_1
  assign Bout6 = AO ? ALUout6 : 1'bz;  // Controlled_Buffer controlled_buffer_2
  assign controlled_buffer_3_out = AI ? Bin7 : 1'bz;  // Controlled_Buffer controlled_buffer_3
  D_Flip_Flop d_ff_1 (.D(controlled_buffer_3_out), .clk(clk), .Q(ALUout7));  // open: Qn, preset, reset
  assign Bout5 = AO ? ALUout5 : 1'bz;  // Controlled_Buffer controlled_buffer_4
  assign controlled_buffer_5_out = AI ? Bin6 : 1'bz;  // Controlled_Buffer controlled_buffer_5
  assign Bout4 = AO ? ALUout4 : 1'bz;  // Controlled_Buffer controlled_buffer_6
  assign controlled_buffer_7_out = AI ? Bin5 : 1'bz;  // Controlled_Buffer controlled_buffer_7
  D_Flip_Flop d_ff_2 (.D(controlled_buffer_5_out), .clk(clk), .Q(ALUout6));  // open: Qn, preset, reset
  assign Bout3 = AO ? ALUout3 : 1'bz;  // Controlled_Buffer controlled_buffer_8
  assign controlled_buffer_9_out = AI ? Bin4 : 1'bz;  // Controlled_Buffer controlled_buffer_9
  D_Flip_Flop d_ff_3 (.D(controlled_buffer_7_out), .clk(clk), .Q(ALUout5));  // open: Qn, preset, reset
  assign Bout2 = AO ? ALUout2 : 1'bz;  // Controlled_Buffer controlled_buffer_10
  assign controlled_buffer_11_out = AI ? Bin3 : 1'bz;  // Controlled_Buffer controlled_buffer_11
  assign Bout1 = AO ? ALUout1 : 1'bz;  // Controlled_Buffer controlled_buffer_12
  assign controlled_buffer_13_out = AI ? Bin2 : 1'bz;  // Controlled_Buffer controlled_buffer_13
  D_Flip_Flop d_ff_4 (.D(controlled_buffer_9_out), .clk(clk), .Q(ALUout4));  // open: Qn, preset, reset
  assign Bout0 = AO ? ALUout0 : 1'bz;  // Controlled_Buffer controlled_buffer_14
  assign controlled_buffer_15_out = AI ? Bin1 : 1'bz;  // Controlled_Buffer controlled_buffer_15
  D_Flip_Flop d_ff_5 (.D(controlled_buffer_11_out), .clk(clk), .Q(ALUout3));  // open: Qn, preset, reset
  assign controlled_buffer_16_out = AI ? Bin0 : 1'bz;  // Controlled_Buffer controlled_buffer_16
  D_Flip_Flop d_ff_6 (.D(controlled_buffer_13_out), .clk(clk), .Q(ALUout2));  // open: Qn, preset, reset
  D_Flip_Flop d_ff_7 (.D(controlled_buffer_15_out), .clk(clk), .Q(ALUout1));  // open: Qn, preset, reset
  D_Flip_Flop d_ff_8 (.D(controlled_buffer_16_out), .clk(clk), .Q(ALUout0));  // open: Qn, preset, reset
endmodule

module ALU (
  input  A7,
  input  A6,
  input  A5,
  input  A4,
  input  A3,
  input  A2,
  input  A1,
  input  A0,
  input  B7,
  input  B6,
  input  B5,
  input  B4,
  input  B3,
  input  B2,
  input  B1,
  input  B0,
  input  EO,
  input  SU,
  output Bo0,
  output Bo1,
  output Bo2,
  output Bo3,
  output Bo4,
  output Bo5,
  output Bo6,
  output Bo7
);

  wire and_1_out, and_2_out, not_1_out;
  wire [7:0] adder_1_out, subtractor_1_out;

  Adder adder_1 (
    .a({A7, A6, A5, A4, A3, A2, A1, A0}), .b({B7, B6, B5, B4, B3, B2, B1, B0}), .out(adder_1_out));  // open: cin, cout
  assign {Bo7, Bo6, Bo5, Bo4, Bo3, Bo2, Bo1, Bo0} = and_1_out ? adder_1_out : 8'bz;  // Controlled_Buffer controlled_buffer_1
  and and_1 (and_1_out, not_1_out, EO);
  not not_1 (not_1_out, SU);
  Subtractor subtractor_1 (
    .a({A7, A6, A5, A4, A3, A2, A1, A0}), .b({B7, B6, B5, B4, B3, B2, B1, B0}), .out(subtractor_1_out));  // open: bin, bout
  and and_2 (and_2_out, SU, EO);
  assign {Bo7, Bo6, Bo5, Bo4, Bo3, Bo2, Bo1, Bo0} = and_2_out ? subtractor_1_out : 8'bz;  // Controlled_Buffer controlled_buffer_2
endmodule

module Bregister (
  input  B7,
  input  B6,
  input  B5,
  input  B4,
  input  B3,
  input  B2,
  input  B1,
  input  B0,
  input  BI,
  input  CLK,
  output A7,
  output A6,
  output A5,
  output A4,
  output A3,
  output A2,
  output A1,
  output A0
);

  wire [7:0] controlled_buffer_1_out;

  assign controlled_buffer_1_out = BI ? {B7, B6, B5, B4, B3, B2, B1, B0} : 8'bz;  // Controlled_Buffer controlled_buffer_1
  Register register_1 (.D(controlled_buffer_1_out), .clk(CLK), .Q({A7, A6, A5, A4, A3, A2, A1, A0}));  // open: en, clr
endmodule

module OutRegister (
  input  B7,
  input  B6,
  input  B5,
  input  B4,
  input  B3,
  input  B2,
  input  B1,
  input  B0,
  input  OI,
  input  CLK,
  input  rst,
  output A7,
  output A6,
  output A5,
  output A4,
  output A3,
  output A2,
  output A1,
  output A0
);

  wire controlled_buffer_1_out, controlled_buffer_2_out, controlled_buffer_3_out, controlled_buffer_4_out,
       controlled_buffer_5_out, controlled_buffer_6_out, controlled_buffer_7_out, controlled_buffer_8_out;

  assign controlled_buffer_1_out = OI ? B6 : 1'bz;  // Controlled_Buffer controlled_buffer_1
  assign controlled_buffer_2_out = OI ? B7 : 1'bz;  // Controlled_Buffer controlled_buffer_2
  D_Flip_Flop d_ff_1 (.D(controlled_buffer_2_out), .clk(CLK), .Q(A7), .reset(rst));  // open: Qn, preset
  assign controlled_buffer_3_out = OI ? B5 : 1'bz;  // Controlled_Buffer controlled_buffer_3
  D_Flip_Flop d_ff_2 (.D(controlled_buffer_1_out), .clk(CLK), .Q(A6), .reset(rst));  // open: Qn, preset
  assign controlled_buffer_4_out = OI ? B4 : 1'bz;  // Controlled_Buffer controlled_buffer_4
  assign controlled_buffer_5_out = OI ? B3 : 1'bz;  // Controlled_Buffer controlled_buffer_5
  D_Flip_Flop d_ff_3 (.D(controlled_buffer_3_out), .clk(CLK), .Q(A5), .reset(rst));  // open: Qn, preset
  assign controlled_buffer_6_out = OI ? B2 : 1'bz;  // Controlled_Buffer controlled_buffer_6
  assign controlled_buffer_7_out = OI ? B1 : 1'bz;  // Controlled_Buffer controlled_buffer_7
  D_Flip_Flop d_ff_4 (.D(controlled_buffer_4_out), .clk(CLK), .Q(A4), .reset(rst));  // open: Qn, preset
  assign controlled_buffer_8_out = OI ? B0 : 1'bz;  // Controlled_Buffer controlled_buffer_8
  D_Flip_Flop d_ff_5 (.D(controlled_buffer_5_out), .clk(CLK), .Q(A3), .reset(rst));  // open: Qn, preset
  D_Flip_Flop d_ff_6 (.D(controlled_buffer_6_out), .clk(CLK), .Q(A2), .reset(rst));  // open: Qn, preset
  D_Flip_Flop d_ff_7 (.D(controlled_buffer_7_out), .clk(CLK), .Q(A1), .reset(rst));  // open: Qn, preset
  D_Flip_Flop d_ff_8 (.D(controlled_buffer_8_out), .clk(CLK), .Q(A0), .reset(rst));  // open: Qn, preset
endmodule

module InsturductionRegister (
  input  B7,
  input  B6,
  input  B5,
  input  B4,
  input  B3,
  input  B2,
  input  B1,
  input  B0,
  input  IO,
  input  II,
  input  CLK,
  input  RST,
  output C3,
  output C2,
  output C1,
  output C0,
  output BUS3,
  output BUS2,
  output BUS1,
  output BUS0
);

  wire [7:0] controlled_buffer_1_out, register_1_q;

  assign controlled_buffer_1_out = II ? {B7, B6, B5, B4, B3, B2, B1, B0} : 8'bz;  // Controlled_Buffer controlled_buffer_1
  Register register_1 (.D(controlled_buffer_1_out), .clk(CLK), .Q(register_1_q), .clr(RST));  // open: en
  assign {C3, C2, C1, C0, BUS3, BUS2, BUS1, BUS0} = IO ? register_1_q : 8'bz;  // Controlled_Buffer controlled_buffer_2
endmodule

module ControllerSequencer (
  input  CLK,
  input  RST,
  input  A3,
  input  A2,
  input  A1,
  input  A0,
  input  HRDRST,
  output HLT,
  output stpclk,
  output CO,
  output CE,
  output II,
  output IO,
  output MI,
  output BI,
  output AO,
  output OI,
  output SU,
  output EO,
  output AI,
  output RO
);

  wire and_2_out, and_3_out, d_ff_1_q, d_ff_2_q, d_ff_3_q, d_ff_4_q, d_ff_10_q, d_ff_11_q, d_ff_12_q,
       demultiplexer_1_out0, demultiplexer_1_out1, demultiplexer_1_out2, demultiplexer_1_out3,
       demultiplexer_1_out14, demultiplexer_1_out15, not_1_out, or_1_out, or_2_out, or_3_out, or_6_out,
       or_8_out, or_9_out, undriven;

  or or_1 (or_1_out, HLT, d_ff_4_q, d_ff_3_q, d_ff_2_q);
  D_Flip_Flop d_ff_1 (.Q(d_ff_1_q), .preset(demultiplexer_1_out0), .reset(or_2_out));  // open: D, clk, Qn
  or or_2 (or_2_out, or_1_out, or_9_out);
  and and_1 (IO, or_3_out, d_ff_10_q);
  Demultiplexer #(.select(4)) demultiplexer_1 (
    .out0(demultiplexer_1_out0), .out1(demultiplexer_1_out1), .out2(demultiplexer_1_out2),
    .out3(demultiplexer_1_out3), .out14(demultiplexer_1_out14), .out15(demultiplexer_1_out15), .in(1'b1),
    .sel({A3, A2, A1, A0}));  // open: out4, out5, out6, out7, out8, out9, out10, out11, out12, out13
  D_Flip_Flop d_ff_2 (.Q(d_ff_2_q), .preset(demultiplexer_1_out1), .reset(or_9_out));  // open: D, clk, Qn
  or or_3 (or_3_out, d_ff_1_q, d_ff_2_q, d_ff_3_q);
  or or_4 (MI, IO, CO);
  D_Flip_Flop d_ff_3 (.Q(d_ff_3_q), .preset(demultiplexer_1_out2), .reset(or_9_out));  // open: D, clk, Qn
  buf and_2 (and_2_out, d_ff_11_q);  // AND_Gate
  D_Flip_Flop d_ff_4 (.Q(d_ff_4_q), .preset(demultiplexer_1_out3), .reset(or_9_out));  // open: D, clk, Qn
  or or_5 (RO, and_2_out, II);
  D_Flip_Flop d_ff_5 (.Q(HLT), .preset(demultiplexer_1_out15), .reset(or_9_out));  // open: D, clk, Qn
  or or_6 (or_6_out, d_ff_2_q, d_ff_3_q);
  and and_3 (and_3_out, d_ff_1_q, d_ff_11_q);
  or or_7 (AI, and_3_out, EO);
  and and_4 (BI, or_6_out, d_ff_11_q);
  not not_1 (not_1_out, or_8_out);
  D_Flip_Flop d_ff_6 (.Q(stpclk), .preset(demultiplexer_1_out14), .reset(HRDRST));  // open: D, clk, Qn
  and and_5 (EO, or_6_out, d_ff_12_q);
  or or_8 (or_8_out, d_ff_11_q, d_ff_10_q, II, CE, CO);
  D_Flip_Flop d_ff_7 (.D(not_1_out), .clk(CLK), .Q(CO), .preset(undriven), .reset(RST));  // open: Qn
  and and_6 (SU, d_ff_3_q, d_ff_12_q);
  D_Flip_Flop d_ff_8 (.D(CO), .clk(CLK), .Q(CE), .reset(RST));  // open: Qn, preset
  or or_9 (or_9_out, CO, RST);
  D_Flip_Flop d_ff_9 (.D(CE), .clk(CLK), .Q(II), .reset(RST));  // open: Qn, preset
  and and_7 (AO, d_ff_4_q, d_ff_10_q);
  D_Flip_Flop d_ff_10 (.D(II), .clk(CLK), .Q(d_ff_10_q), .reset(RST));  // open: Qn, preset
  D_Flip_Flop d_ff_11 (.D(d_ff_10_q), .clk(CLK), .Q(d_ff_11_q), .reset(RST));  // open: Qn, preset
  D_Flip_Flop d_ff_12 (.D(d_ff_11_q), .clk(CLK), .Q(d_ff_12_q), .reset(RST));  // open: Qn, preset

  assign OI = AO;

  // Notes on the sheet:
  //   SUB
  //   OUT
  //   HLT
endmodule
